// Digital circuit Controller.dig as structural Verilog
// The program counter.
// Here the current program counter is stored.
// The various inputs can be used to influence how the 
// program counter is modified if a clock signal happens.
// {{de Der Programmzähler. 
// Hier wird der aktuelle Programmzähler gespeichert. 
// Über die verschiedenen Eingänge kann beeinflußt 
// werden, auf welche Weise der Programmzähler mit 
// dem Takt weiter geschaltet wird.}}
module Controller (
  input  [31:0] instr,
  input  Zero,
  output [1:0] PCSrc,
  output [3:0] ALUControl,
  output ASrc,
  output ALUSrc,
  output [1:0] ResultSrc,
  output MemWrite,
  output RegWrite
);

  wire u_controldec_branch, u_controldec_jalr, u_controldec_jump;

  controldec #(.applicationType("IVERILOG"), .iverilogOptions("-g2012")) u_controldec (
    .instr(instr), .RegWrite(RegWrite), .MemWrite(MemWrite), .ResultSrc(ResultSrc), .ALUSrc(ALUSrc),
    .ASrc(ASrc), .ALUControl(ALUControl), .Branch(u_controldec_branch), .Jump(u_controldec_jump),
    .Jalr(u_controldec_jalr));
  branchlogic #(.applicationType("IVERILOG"), .iverilogOptions("-g2012")) u_branchlogic (
    .Branch(u_controldec_branch), .Jump(u_controldec_jump), .Jalr(u_controldec_jalr), .funct3(instr[14:12]),
    .Zero(Zero), .PCSrc(PCSrc));
endmodule

/* Code of controldec:
module controldec (
  input  logic [31:0] instr,
  output logic        RegWrite, MemWrite, Branch, Jump, Jalr,
  output logic [1:0]  ResultSrc,
  output logic        ALUSrc, ASrc,
  output logic [3:0]  ALUControl
);

  always_comb begin
    // Valores por defecto
    RegWrite   = 0;
    MemWrite   = 0;
    Branch     = 0;
    Jump       = 0;
    Jalr       = 0;
    ResultSrc  = 2'b00;
    ALUSrc     = 0;
    ASrc       = 0;       // 0: primer operando de la ALU es rs1, 1: es el PC
    ALUControl = 4'b0000;

    case (instr[6:0])
      // R-type e I-type aritmética: misma decodificación de funct3
      7'b0110011, 7'b0010011: begin
        RegWrite   = 1;
        ResultSrc  = 2'b00;   // ALUResult
        ALUSrc     = ~instr[5]; // 0 en tipo R (registro), 1 en tipo I (inmediato)
        case (instr[14:12])
          3'b000: ALUControl = (instr[5] & instr[30]) ? 4'b0001 : 4'b0000; // sub o add/addi
          3'b001: ALUControl = 4'b1001;                                     // sll, slli
          3'b010: ALUControl = 4'b0101;                                     // slt, slti
          3'b011: ALUControl = 4'b1100;                                     // sltu, sltiu
          3'b100: ALUControl = 4'b1000;                                     // xor, xori
          3'b101: ALUControl = instr[30] ? 4'b1011 : 4'b1010;               // sra/srai o srl/srli
          3'b110: ALUControl = 4'b0011;                                     // or, ori
          3'b111: ALUControl = 4'b0010;                                     // and, andi
        endcase
      end

      // I-type (load)
      7'b0000011: begin
        RegWrite   = 1;
        ResultSrc  = 2'b01;   // ReadData
        ALUSrc     = 1;       // segundo operando de la ALU viene de la extensión inmediata
        ALUControl = 4'b0000; // add (para calcular la dirección)
      end

      // S-type (store)
      7'b0100011: begin
        MemWrite   = 1;
        ALUSrc     = 1;       // segundo operando de la ALU viene de la extensión inmediata
        ALUControl = 4'b0000; // add (para calcular la dirección)
      end

      // B-type (branch): la ALU compara rs1 y rs2; el controller decide
      // con Zero y funct3 si se salta
      7'b1100011: begin
        Branch     = 1;
        ALUSrc     = 0;       // segundo operando de la ALU viene del registro
        case (instr[14:13])
          2'b00:   ALUControl = 4'b0001; // beq, bne: sub (Zero = iguales)
          2'b10:   ALUControl = 4'b0101; // blt, bge: slt (Zero = no menor con signo)
          2'b11:   ALUControl = 4'b1100; // bltu, bgeu: sltu (Zero = no menor sin signo)
          default: ALUControl = 4'b0001; // funct3 = 01x no existe
        endcase
      end

      // U-type (lui): rd = inmediato U, sin pasar por la ALU
      7'b0110111: begin
        RegWrite   = 1;
        ResultSrc  = 2'b11;   // ImmExt
      end

      // U-type (auipc): rd = PC + inmediato U, calculado en la ALU
      7'b0010111: begin
        RegWrite   = 1;
        ResultSrc  = 2'b00;   // ALUResult
        ASrc       = 1;       // primer operando de la ALU es el PC
        ALUSrc     = 1;       // segundo operando de la ALU es la extensión inmediata
        ALUControl = 4'b0000; // add
      end

      // J-type (jal)
      7'b1101111: begin
        RegWrite   = 1;
        ResultSrc  = 2'b10;   // PC+4
        Jump       = 1;
      end

      // I-type (jalr): rd = PC+4, PC = (rs1 + inmediato) & ~1, calculado en la ALU
      7'b1100111: begin
        RegWrite   = 1;
        ResultSrc  = 2'b10;   // PC+4
        ALUSrc     = 1;       // segundo operando de la ALU es la extensión inmediata
        ALUControl = 4'b0000; // add
        Jalr       = 1;
      end
    endcase
  end
endmodule
*/

/* Code of branchlogic:
module branchlogic (
  input  logic [2:0] funct3,
  input  logic        Zero, Branch, Jump, Jalr,
  output logic [1:0]  PCSrc       // 00: PC+4, 01: PC+inmediato (branch, jal), 10: ALUResult (jalr)
);

  logic Taken;                 // se cumple la condición del salto condicional

  // Condición de salto según funct3 (la ALU ya ha hecho sub, slt o sltu)
  always_comb begin
    case (funct3)
      3'b000:  Taken =  Zero;   // beq:  rs1 == rs2
      3'b001:  Taken = ~Zero;   // bne:  rs1 != rs2
      3'b100:  Taken = ~Zero;   // blt:  slt = 1
      3'b101:  Taken =  Zero;   // bge:  slt = 0
      3'b110:  Taken = ~Zero;   // bltu: sltu = 1
      3'b111:  Taken =  Zero;   // bgeu: sltu = 0
      default: Taken = 1'b0;
    endcase
  end

  assign PCSrc = Jalr ? 2'b10 : {1'b0, Jump | (Branch & Taken)};
endmodule
*/
