// Digital circuit P3.dig as structural Verilog
// The program counter.
// Here the current program counter is stored.
// The various inputs can be used to influence how the 
// program counter is modified if a clock signal happens.
// {{de Der Programmzähler. 
// Hier wird der aktuelle Programmzähler gespeichert. 
// Über die verschiedenen Eingänge kann beeinflußt 
// werden, auf welche Weise der Programmzähler mit 
// dem Takt weiter geschaltet wird.}}
module P3 (
  input  CLK,
  input  Rst
);

  wire [3:0] undriven;

  D_FF_AS #(.Bits(32)) PC (.Set(1'b0), .C(CLK), .Clr(Rst));  // open: D, Q, nQ
  ROM #(.AddrBits(10), .Bits(32)) MemoInstr ();  // open: A, sel, D
  extend #(.applicationType("IVERILOG"), .iverilogOptions("-g2012")) u_extend ();  // open: instr, immext
  Controller controller_1 ();  // open: instr, Zero, PCSrc, ALUControl, ASrc, ALUSrc, ResultSrc, MemWrite, RegWrite
  alu #(.applicationType("IVERILOG"), .iverilogOptions("-g2012")) u_alu (.alucontrol(undriven));  // open: a, b, zero, result
  storealign #(.applicationType("IVERILOG"), .iverilogOptions("-g2012")) u_storealign ();  // open: funct3, addr, rs2_data, byte_en, write_data
  loadext #(.applicationType("IVERILOG"), .iverilogOptions("-g2012")) u_loadext ();  // open: funct3, addr, mem_data, read_data

  // Notes on the sheet:
  //   MemoInstr loads prueba_completa.hex
endmodule

/* Code of extend:
module extend (
    input  logic [31:0] instr,
    output logic [31:0] immext
);

  always_comb begin
    case (instr[6:0])
      7'b0010011, 7'b0000011, 7'b1100111:
        immext = {{20{instr[31]}}, instr[31:20]};                                           // I
      7'b0100011:
        immext = {{20{instr[31]}}, instr[31:25], instr[11:7]};                              // S
      7'b1100011:
        immext = {{19{instr[31]}}, instr[31], instr[7], instr[30:25], instr[11:8], 1'b0};   // B
      7'b0110111, 7'b0010111:
        immext = {instr[31:12], 12'b0};                                                     // U
      7'b1101111:
        immext = {{11{instr[31]}}, instr[31], instr[19:12], instr[20], instr[30:21], 1'b0}; // J
      default:
        immext = '0;
    endcase
  end
endmodule
*/

/* Code of alu:
module alu_shifter (
    input  logic [31:0] a,
    input  logic [4:0]  shamt,
    input  logic [3:0]  alucontrol,
    output logic [31:0] y
);

  always_comb begin
    case (alucontrol)
      4'b1001: y = a << shamt;            // SLL
      4'b1010: y = a >> shamt;            // SRL
      4'b1011: y = $signed(a) >>> shamt;  // SRA
      default: y = 32'h0;
    endcase
  end

endmodule

// ---------------------------------------------------------------------
// Comparador: SLT, SLTU
// ---------------------------------------------------------------------
module alu_cmp (
    input  logic [31:0] a,
    input  logic [31:0] b,
    input  logic [3:0]  alucontrol,
    output logic [31:0] y
);

  always_comb begin
    case (alucontrol)
      4'b0101: y = {31'b0, $signed(a) < $signed(b)};  // SLT
      4'b1100: y = {31'b0, a < b};                    // SLTU
      default: y = 32'h0;
    endcase
  end

endmodule

// ---------------------------------------------------------------------
// ALU: el case solo selecciona el resultado
// ---------------------------------------------------------------------
module alu (
    input  logic [31:0] a,
    input  logic [31:0] b,
    input  logic [3:0]  alucontrol,
    output logic [31:0] result,
    output logic        zero
);

  logic [31:0] shift_res, cmp_res;

  alu_shifter u_shifter (
      .a         (a),
      .shamt     (b[4:0]),
      .alucontrol(alucontrol),
      .y         (shift_res)   // salida del módulo de desplazamiento
  );

  alu_cmp u_cmp (
      .a         (a),
      .b         (b),
      .alucontrol(alucontrol),
      .y         (cmp_res)    // salida del módulo de comparación
  );

  always_comb begin
    case (alucontrol)

      4'b0000: result = a + b;            // ADD
      4'b0001: result = a - b;            // SUB
      4'b0010: result = a & b;            // AND
      4'b0011: result = a | b;            // OR
      4'b1000: result = a ^ b;            // XOR

      4'b0101,                            // SLT
      4'b1100: result = cmp_res;          // SLTU Salida del módulo de comparación

      4'b1001,                            // SLL
      4'b1010,                            // SRL
      4'b1011: result = shift_res;        // SRA  Salida del módulo de desplazamiento

      default: result = 32'hDEADBEEF;     // valor por defecto para depuración
    endcase
  end

  assign zero = (result == 32'h0);

endmodule
*/

/* Code of storealign:
module storealign (
  input  logic [2:0]  funct3,      // 000: sb, 001: sh, 010: sw
  input  logic [1:0]  addr,        // dos bits bajos de la dirección
  input  logic [31:0] rs2_data,
  output logic [31:0] write_data,
  output logic [3:0]  byte_en
);

  always_comb begin
    case (funct3[1:0])
      2'b00: begin   // sb
        write_data = {4{rs2_data[7:0]}};
        byte_en    = 4'b0001 << addr;
      end
      2'b01: begin   // sh (addr[0] se ignora: accesos no alineados no soportados)
        write_data = {2{rs2_data[15:0]}};
        byte_en    = addr[1] ? 4'b1100 : 4'b0011;
      end
      default: begin // sw
        write_data = rs2_data;
        byte_en    = 4'b1111;
      end
    endcase
  end
endmodule
*/

/* Code of loadext:
module loadext (
  input  logic [2:0]  funct3,      // 000: lb, 001: lh, 010: lw, 100: lbu, 101: lhu
  input  logic [1:0]  addr,        // dos bits bajos de la dirección
  input  logic [31:0] mem_data,
  output logic [31:0] read_data
);

  logic [7:0]  byte_sel;
  logic [15:0] half_sel;

  assign byte_sel = mem_data[8*addr +: 8];
  assign half_sel = addr[1] ? mem_data[31:16] : mem_data[15:0];   // addr[0] se ignora

  always_comb begin
    case (funct3)
      3'b000:  read_data = {{24{byte_sel[7]}},  byte_sel};   // lb
      3'b001:  read_data = {{16{half_sel[15]}}, half_sel};   // lh
      3'b100:  read_data = {24'b0, byte_sel};                // lbu
      3'b101:  read_data = {16'b0, half_sel};                // lhu
      default: read_data = mem_data;                         // lw
    endcase
  end
endmodule
*/
